# Fritzing sketch pcb (saved by Fritzing 0.9.3b)
circuit board: 22.6181cm x 13.123cm
breadboards: 1

parts:
  U1 = 74HC595 [package="DIP16 [THT]"]
  U2 = 74HC595 [package="DIP16 [THT]"]
  U3 = 74HC595 [package="DIP16 [THT]"]
  R2 = Resistor [tolerance=±5% resistance=220 package=THT]
  R3 = Resistor [tolerance=±5% resistance=220 package=THT]
  R4 = Resistor [tolerance=±5% resistance=220 package=THT]
  R5 = Resistor [tolerance=±5% resistance=220 package=THT]
  R6 = Resistor [tolerance=±5% resistance=220 package=THT]
  R7 = Resistor [tolerance=±5% resistance=220 package=THT]
  R8 = Resistor [tolerance=±5% resistance=220 package=THT]
  R9 = Resistor [tolerance=±5% resistance=220 package=THT]
  R10 = Resistor [tolerance=±5% resistance=220 package=THT]
  R11 = Resistor [tolerance=±5% resistance=220 package=THT]
  R12 = Resistor [tolerance=±5% resistance=220 package=THT]
  R13 = Resistor [tolerance=±5% resistance=220 package=THT]
  R14 = Resistor [tolerance=±5% resistance=220 package=THT]
  R15 = Resistor [tolerance=±5% resistance=220 package=THT]
  R16 = Resistor [tolerance=±5% resistance=220 package=THT]
  R1 = Resistor [tolerance=±5% resistance=1.5k package=THT]
  R17 = Resistor [tolerance=±5% resistance=1.5k package=THT]
  R18 = Resistor [tolerance=±5% resistance=1.5k package=THT]
  R19 = Resistor [tolerance=±5% resistance=1.5k package=THT]
  R20 = Resistor [tolerance=±5% resistance=1.5k package=THT]
  R21 = Resistor [tolerance=±5% resistance=1.5k package=THT]
  R22 = Resistor [tolerance=±5% resistance=1.5k package=THT]
  R23 = Resistor [tolerance=±5% resistance=1.5k package=THT]
  R24 = Resistor [tolerance=±5% resistance=1.5k package=THT]
  U4 = atmega328 [package=dip]
  XTAL1 = Crystal [frequency="16 Mhz" package=THT]
  C1 = Capacitor [package=cap-pth-small]
  C2 = Capacitor [package=cap-pth-small]
  S2 = Pushbutton [package="[THT]"]
  S3 = SPST Switch [package=switch-spdt_kit]
  S4 = SPST Switch [package=switch-spdt_kit]
  S5 = SPST Switch [package=switch-spdt_kit]
  S6 = SPST Switch [package=switch-spdt_kit]
  S7 = SPST Switch [package=switch-spdt_kit]
  S8 = SPST Switch [package=switch-spdt_kit]
  S9 = SPST Switch [package=switch-spdt_kit]
  S10 = SPST Switch [package=switch-spdt_kit]
  LED2 = LED - 5mm [color="Red (633nm)" package="5 mm [THT]"]
  LED3 = LED - 5mm [color="Red (633nm)" package="5 mm [THT]"]
  LED4 = LED - 5mm [color="Red (633nm)" package="5 mm [THT]"]
  LED5 = LED - 5mm [color="Red (633nm)" package="5 mm [THT]"]
  LED6 = LED - 5mm [color="Red (633nm)" package="5 mm [THT]"]
  LED7 = LED - 5mm [color="Red (633nm)" package="5 mm [THT]"]
  LED8 = LED - 5mm [color="Red (633nm)" package="5 mm [THT]"]
  LED9 = LED - 5mm [color="Red (633nm)" package="5 mm [THT]"]
  R25 = Resistor [tolerance=±5% resistance=1.5k package=THT]
  R26 = Resistor [tolerance=±5% resistance=1.5k package=THT]
  R27 = Resistor [tolerance=±5% resistance=1.5k package=THT]
  R28 = Resistor [tolerance=±5% resistance=1.5k package=THT]
  R29 = Resistor [tolerance=±5% resistance=1.5k package=THT]
  R30 = Resistor [tolerance=±5% resistance=1.5k package=THT]
  R31 = Resistor [tolerance=±5% resistance=1.5k package=THT]
  R32 = Resistor [tolerance=±5% resistance=1.5k package=THT]
  S11 = Pushbutton [package="[THT]"]
  S12 = Pushbutton [package="[THT]"]
  S13 = Pushbutton [package="[THT]"]
  S14 = Pushbutton [package="[THT]"]
  S15 = Pushbutton [package="[THT]"]
  S16 = Pushbutton [package="[THT]"]
  S17 = Pushbutton [package="[THT]"]
  R33 = Resistor [tolerance=±5% resistance=1.5k package=THT]
  R34 = Resistor [tolerance=±5% resistance=1.5k package=THT]
  R35 = Resistor [tolerance=±5% resistance=1.5k package=THT]
  R36 = Resistor [tolerance=±5% resistance=1.5k package=THT]
  R37 = Resistor [tolerance=±5% resistance=1.5k package=THT]
  R38 = Resistor [tolerance=±5% resistance=1.5k package=THT]
  R39 = Resistor [tolerance=±5% resistance=1.5k package=THT]
  R40 = Resistor [tolerance=±5% resistance=1.5k package=THT]
  S18 = SPST Switch [package=switch-spdt_kit]
  S19 = SPST Switch [package=switch-spdt_kit]
  S20 = SPST Switch [package=switch-spdt_kit]
  S21 = SPST Switch [package=switch-spdt_kit]
  S22 = SPST Switch [package=switch-spdt_kit]
  S23 = SPST Switch [package=switch-spdt_kit]
  S24 = SPST Switch [package=switch-spdt_kit]
  S25 = SPST Switch [package=switch-spdt_kit]
  LED10 = LED - 5mm [color="Red (633nm)" package="5 mm [THT]"]
  LED11 = LED - 5mm [color="Red (633nm)" package="5 mm [THT]"]
  LED12 = LED - 5mm [color="Red (633nm)" package="5 mm [THT]"]
  LED13 = LED - 5mm [color="Red (633nm)" package="5 mm [THT]"]
  LED14 = LED - 5mm [color="Red (633nm)" package="5 mm [THT]"]
  LED15 = LED - 5mm [color="Red (633nm)" package="5 mm [THT]"]
  LED16 = LED - 5mm [color="Red (633nm)" package="5 mm [THT]"]
  LED17 = LED - 5mm [color="Red (633nm)" package="5 mm [THT]"]
  LED18 = LED - 5mm [color="Red (633nm)" package="5 mm [THT]"]  # not connected
  LED19 = LED - 5mm [color="Red (633nm)" package="5 mm [THT]"]  # not connected
  LED20 = LED - 5mm [color="Red (633nm)" package="5 mm [THT]"]  # not connected
  LED21 = LED - 5mm [color="Red (633nm)" package="5 mm [THT]"]  # not connected
  LED22 = LED - 5mm [color="Red (633nm)" package="5 mm [THT]"]  # not connected
  LED23 = LED - 5mm [color="Red (633nm)" package="5 mm [THT]"]  # not connected
  LED24 = LED - 5mm [color="Red (633nm)" package="5 mm [THT]"]  # not connected
  LED25 = LED - 5mm [color="Red (633nm)" package="5 mm [THT]"]  # not connected
  LED26 = LED - 5mm [color="Red (633nm)" package="5 mm [THT]"]  # not connected
  LED27 = LED - 5mm [color="Red (633nm)" package="5 mm [THT]"]  # not connected
  LED28 = LED - 5mm [color="Red (633nm)" package="5 mm [THT]"]  # not connected
  LED29 = LED - 5mm [color="Red (633nm)" package="5 mm [THT]"]  # not connected
  LED30 = LED - 5mm [color="Red (633nm)" package="5 mm [THT]"]  # not connected
  LED31 = LED - 5mm [color="Red (633nm)" package="5 mm [THT]"]  # not connected
  LED32 = LED - 5mm [color="Red (633nm)" package="5 mm [THT]"]  # not connected
  LED33 = LED - 5mm [color="Red (633nm)" package="5 mm [THT]"]  # not connected
  R41 = Resistor [tolerance=±5% resistance=1.5k package=THT]  # not connected
  R42 = Resistor [tolerance=±5% resistance=1.5k package=THT]  # not connected
  R43 = Resistor [tolerance=±5% resistance=1.5k package=THT]  # not connected
  R44 = Resistor [tolerance=±5% resistance=1.5k package=THT]  # not connected
  R45 = Resistor [tolerance=±5% resistance=1.5k package=THT]  # not connected
  R46 = Resistor [tolerance=±5% resistance=1.5k package=THT]  # not connected
  R47 = Resistor [tolerance=±5% resistance=1.5k package=THT]  # not connected
  R48 = Resistor [tolerance=±5% resistance=1.5k package=THT]  # not connected
  R49 = Resistor [tolerance=±5% resistance=1.5k package=THT]  # not connected
  R50 = Resistor [tolerance=±5% resistance=1.5k package=THT]  # not connected
  R51 = Resistor [tolerance=±5% resistance=1.5k package=THT]  # not connected
  R52 = Resistor [tolerance=±5% resistance=1.5k package=THT]  # not connected
  R53 = Resistor [tolerance=±5% resistance=1.5k package=THT]  # not connected
  R54 = Resistor [tolerance=±5% resistance=1.5k package=THT]  # not connected
  R55 = Resistor [tolerance=±5% resistance=1.5k package=THT]  # not connected
  R57 = Resistor [tolerance=±5% resistance=1.5k package=THT]  # not connected

nets:
  N1: U1.Q1, U2.Q1, U3.Q1, U4.D13
  N2: U1.Q2, U2.Q2, U3.Q2, U4.D12
  N3: U1.Q3, R1.Pin_0, LED13.anode
  N4: U1.Q4, R2.Pin_0, LED10.anode
  N5: U1.Q5, R3.Pin_0, LED11.anode
  N6: U1.Q6, R4.Pin_0, LED14.anode
  GND: U1.GND, U1.Q0, U2.GND, U2.Q0, U3.GND, U3.Q0, R2.Pin_1, R3.Pin_1, R4.Pin_1, R5.Pin_1, R6.Pin_1, R7.Pin_1, R8.Pin_1, R9.Pin_1, R10.Pin_1, R11.Pin_1, R12.Pin_1, R13.Pin_1, R14.Pin_1, R15.Pin_1, R16.Pin_1, R1.Pin_1, R21.Pin_1, R22.Pin_1, R23.Pin_1, R24.Pin_1, U4.GND, C1.2, C2.2
  N7: U1.Q7', U2.MR
  N8: U1.SH_CP, R20.Pin_0, LED12.anode
  N9: U1.ST_CP, R19.Pin_0, LED17.anode
  N10: U1.OE, R18.Pin_0, LED15.anode
  N11: U1.DS, R17.Pin_0, LED16.anode
  VCC: U1.VCC, U2.VCC, U4.VCC, U4.AVCC
  N12: U2.Q3, R9.Pin_0, S16.Pin_3
  N13: U2.Q4, R10.Pin_0, S11.Pin_3, S11.Pin_4
  N14: U2.Q5, R11.Pin_0, S15.Pin_3, S15.Pin_4
  N15: U2.Q6, R12.Pin_0, S12.Pin_3, S12.Pin_4
  N16: U2.Q7', U3.MR
  N17: U2.SH_CP, R5.Pin_0, S17.Pin_3, S17.Pin_4
  N18: U2.ST_CP, R6.Pin_0, S13.Pin_3, S13.Pin_4
  N19: U2.OE, R7.Pin_0, S14.Pin_3, S14.Pin_4
  N20: U2.DS, R8.Pin_0, S2.Pin_3, S2.Pin_4
  N21: U3.Q3, R23.Pin_0, LED6.anode
  N22: U3.Q4, R22.Pin_0, LED7.anode
  N23: U3.Q5, R21.Pin_0, LED8.anode
  N24: U3.Q6, R24.Pin_0, LED9.anode
  N25: U3.Q7', U4.D11_(PWM)
  N26: U3.SH_CP, R13.Pin_0, LED3.anode
  N27: U3.ST_CP, R14.Pin_0, LED2.anode
  N28: U3.OE, R15.Pin_0, LED4.anode
  N29: U3.DS, R16.Pin_0, LED5.anode
  N30: U4.XLAT1, XTAL1.pin_0, C2.1
  N31: U4.XLAT2, XTAL1.pin_1, C1.1
  N32: S2.Pin_1, S2.Pin_2, R25.Pin_0, R26.Pin_0, R27.Pin_0, R28.Pin_0, R29.Pin_0, R30.Pin_0, R31.Pin_0, R32.Pin_0, S11.Pin_1, S11.Pin_2, S12.Pin_1, S12.Pin_2, S13.Pin_1, S13.Pin_2, S14.Pin_1, S14.Pin_2, S15.Pin_1, S15.Pin_2, S16.Pin_1, S16.Pin_2, S17.Pin_1, R33.Pin_0, R34.Pin_0, R35.Pin_0, R36.Pin_0, R37.Pin_0, R38.Pin_0, R39.Pin_0, R40.Pin_0
  N33: S3.O, LED8.cathode
  N34: S3.S, R31.Pin_1
  N35: S4.O, LED7.cathode
  N36: S4.S, R30.Pin_1
  N37: S5.O, LED9.cathode
  N38: S5.S, R32.Pin_1
  N39: S6.O, LED6.cathode
  N40: S6.S, R29.Pin_1
  N41: S7.O, LED4.cathode
  N42: S7.S, R27.Pin_1
  N43: S8.O, LED2.cathode
  N44: S8.S, R26.Pin_1
  N45: S9.O, LED3.cathode
  N46: S9.S, R25.Pin_1
  N47: S10.O, LED5.cathode
  N48: S10.S, R28.Pin_1
  N49: R33.Pin_1, S19.S
  N50: R34.Pin_1, S18.S
  N51: R35.Pin_1, S23.S
  N52: R36.Pin_1, S24.S
  N53: R37.Pin_1, S20.S
  N54: R38.Pin_1, S21.S
  N55: R39.Pin_1, S25.S
  N56: R40.Pin_1, S22.S
  N57: S18.O, LED11.cathode
  N58: S19.O, LED10.cathode
  N59: S20.O, LED13.cathode
  N60: S21.O, LED16.cathode
  N61: S22.O, LED17.cathode
  N62: S23.O, LED15.cathode
  N63: S24.O, LED12.cathode
  N64: S25.O, LED14.cathode
